# Fritzing sketch esquematico (saved by Fritzing 0.9.1b)
breadboards: 1

parts:
  R1 = Resistor [tolerance=±5% resistance=1k package=THT]
  Part1 = Arduino Uno (Rev3)
  Q1 = Basic FET N-Channel [package="TO220 [THT]"]
  R2 = Resistor [tolerance=±5% resistance=1k package=THT]
  Q2 = Basic FET N-Channel [package="TO220 [THT]"]
  R3 = Resistor [tolerance=±5% resistance=1k package=THT]
  Q3 = Basic FET N-Channel [package="TO220 [THT]"]
  J2 = female pin header, 2 pins [form="♀ (female)"]
  J3 = female pin header, 2 pins [form="♀ (female)"]
  J1 = female pin header, 2 pins [form="♀ (female)"]

nets:
  N1: R1.Pin_0, Part1.D9_PWM
  N2: R1.Pin_1, Q1.gate
  N3: Part1.D10_PWM/SS, R2.Pin_0
  N4: Part1.D11_PWM/MOSI, R3.Pin_0
  GND: Part1.GND, Q1.source, Q2.source, Q3.source
  N5: Q1.drain, J1.pin2
  N6: R2.Pin_1, Q2.gate
  N7: Q2.drain, J2.pin2
  N8: R3.Pin_1, Q3.gate
  N9: Q3.drain, J3.pin2
  12V: J2.pin1, J3.pin1, J1.pin1

notes:
  +
  -
  led strip 3
  led strip 2
  led strip 1
  Q1 = Q2 = Q3= IRF640
  Terra da fonte conectado ao GND do Arduino
